# Fritzing sketch schematic (saved by Fritzing 0.9.4)
circuit board: 7.83264cm x 5.24259cm
breadboards: 1

parts:
  Micro_principal = Arduino Nano (Rev3.0)
  R2 = Resistor [tolerance=±5% resistance=220 package=THT]
  LED1 = LED - 5mm [color="Green (570nm)" package="5 mm [THT]"]
  LED2 = LED - 5mm [color="Red (633nm)" package="5 mm [THT]"]
  R3 = Resistor [tolerance=±5% resistance=220 package=THT]
  Alim_5V_/_1A = Power plug
  LEDs_Dessus = JST-VHR-3N [part_number=JST-VHR-3N package=THT]
  Bouton_sélecteur = Pushbutton [package="[THT]"]
  Interrupteur_ON/OFF = Toggle Switch [package=THT]
  LEDs_BAS = JST-VHR-3N [part_number=JST-VHR-3N package=THT]
  LEDs_HAUT = JST-VHR-3N [part_number=JST-VHR-3N package=THT]

nets:
  GND: Micro_principal.GND, LED1.cathode, LED2.cathode, Alim_5V_/_1A.GND, LEDs_Dessus.pin1, LEDs_Dessus.pin_4, Bouton_sélecteur.Pin_1, Bouton_sélecteur.Pin_2, LEDs_BAS.pin1, LEDs_BAS.pin_4, LEDs_HAUT.pin1, LEDs_HAUT.pin_4
  N1: Micro_principal.D2, R2.Pin_1
  N2: Micro_principal.D3, Bouton_sélecteur.Pin_4
  N3: Micro_principal.D6, LEDs_HAUT.pin2, LEDs_HAUT.pin_5
  N4: Micro_principal.D7, LEDs_BAS.pin2, LEDs_BAS.pin_5
  N5: Micro_principal.D8, LEDs_Dessus.pin2, LEDs_Dessus.pin_5
  N6: Micro_principal.5V, R3.Pin_0, LEDs_Dessus.pin3, LEDs_Dessus.pin_6, Interrupteur_ON/OFF.L2, LEDs_BAS.pin3, LEDs_BAS.pin_6, LEDs_HAUT.pin3, LEDs_HAUT.pin_6
  N7: R2.Pin_0, LED1.anode
  N8: LED2.anode, R3.Pin_1
  N9: Alim_5V_/_1A.VCC, Interrupteur_ON/OFF.COM
