# Fritzing sketch sonnette (saved by Fritzing 0.9.4)
circuit board: 6.46339cm x 6.50402cm
breadboards: 1

parts:
  R3 = Resistor [tolerance=±5% resistance=10k package=THT]
  C1 = Capacitor Polarized [package=cpol-radial-10uf-25v]
  R5 = Resistor [tolerance=±5% resistance=10 package=THT]
  J1 = Camdenboss CTB0158-2 [part_number=CTB0158-2 package=THT]
  JP1 = Header 4 [package=screwterminal-3.5mm-4_lock]
  R2 = Resistor [tolerance=±5% resistance=50 package=THT]
  D3 = Schottky Diode [part_number=1N5817 package="300 mil [THT]"]
  R1 = Resistor [tolerance=±5% resistance=220 package=THT]
  Q1 = TRANSISTOR_NPN [package=to-92]
  LED1 = LED - 3mm [color="Red (633nm)" package="3 mm [THT]"]
  D2 = Schottky Diode [part_number=1N5817 package="300 mil [THT]"]
  U2 = NodeMCU V1.0
  SG1 = Buzzer 12mm [package=buzzer-12mm]
  R4 = Resistor [tolerance=±5% resistance=10k package=THT]
  R6 = Resistor [tolerance=±5% resistance=220 package=THT]
  LED2 = LED - 3mm [color="Green (565nm)" package="3 mm [THT]"]
  R7 = Resistor [tolerance=±5% resistance=10k package=THT]
  R8 = Resistor [tolerance=±5% resistance=10k package=THT]
  C2 = Capacitor Polarized [package=cpol-radial-10uf-25v]
  D1 = Rectifier Diode [part_number=1N4001 package="300 mil [THT]"]
  S1 = Pushbutton [package="[THT]"]
  S2 = Toggle Switch [package=THT]

nets:
  3.3V: R3.Pin_0, D2.cathode, U2.3V3, R4.Pin_0, R7.Pin_0, R8.Pin_0
  N1: R3.Pin_1, R5.Pin_0, D2.anode, U2.D5
  5V: C1.+, J1.pin2, JP1.1, U2.Vin, SG1.1, C2.+, D1.cathode
  GND: C1.-, J1.pin1, JP1.4, Q1.E, LED1.cathode, U2.GND, LED2.cathode, C2.-, S1.Pin_1, S1.Pin_2, S2.L2
  N2: R5.Pin_1, JP1.3
  N3: JP1.2, D3.cathode
  N4: R2.Pin_0, Q1.B
  N5: R2.Pin_1, U2.D1
  N6: D3.anode, U2.D2, R4.Pin_1
  N7: R1.Pin_0, LED1.anode
  N8: R1.Pin_1, U2.D3
  N9: Q1.C, SG1.2, D1.anode
  N10: U2.D4, R6.Pin_1
  N11: U2.D6, R7.Pin_1, S1.Pin_3, S1.Pin_4
  N12: U2.D7, R8.Pin_1, S2.COM
  N13: R6.Pin_0, LED2.anode

custom parts:
  NodeMCU V1.0: ESP8266 based NodeMCU
